// Logisim project P0.circ as structural Verilog: 4 circuits, main circuit main
module main (
  input  [1:0] In,
  input  CLR,
  output Z
);

  wire CLK_out, multiplexer_1_out;

  Clock CLK (.out(CLK_out));
  Multiplexer multiplexer_1 (.in0(1'b0), .in1(CLK_out), .out(multiplexer_1_out), .sel(CLR));  // open: en
  Register #(.width(2)) register_1 (.D(In), .clk(CLK_out), .clr(multiplexer_1_out));  // open: en, Q
endmodule

module bfsm (
  input  [1:0] in_1,
  output F
);

  wire and_1_out, clock_1_out, not_1_out, register_1_q, undriven;

  Clock clock_1 (.out(clock_1_out));
  and and_1 (and_1_out, in_1[0], not_1_out);
  not not_1 (not_1_out, in_1[1]);
  Register #(.width(1)) register_1 (.D(undriven), .Q(register_1_q), .clk(clock_1_out));  // open: en, clr
endmodule

module acfsm (
  input  [1:0] in_1,
  input  CLR,
  output out_3
);

  wire and_1_out, and_2_out, clock_1_out, not_1_out, not_2_out, not_3_out, or_1_out, register_1_q;

  not not_1 (not_1_out, in_1[0]);
  not not_2 (not_2_out, in_1[1]);
  not not_3 (not_3_out, in_1[0]);
  Clock clock_1 (.out(clock_1_out));
  and and_1 (and_1_out, not_1_out, not_2_out);
  or or_1 (or_1_out, and_1_out, and_2_out);
  and and_2 (and_2_out, not_3_out, in_1[1]);
  Register #(.width(1)) register_1 (.D(or_1_out), .Q(register_1_q), .clk(clock_1_out), .clr(CLR));  // open: en
  and and_3 (out_3, register_1_q, or_1_out);
endmodule

module TST (
  input  S1,
  input  S2,
  input  I,
  output S11,
  output S21,
  output F
);

  wire not_1_out;

  not not_1 (not_1_out, S2);
  and and_1 (F, S2, I);
  and and_2 (S21, not_1_out, I);

  assign S11 = S1;
endmodule
