// Logisim project P0Q1CRC.circ as structural Verilog: 2 circuits, main circuit CRC
module CRC (
  input  [7:0] in_1,
  input  [3:0] in_2,
  output [10:0] out_3
);

  wire [2:0] \四位除数_1_c0 , \四位除数_2_c0 , \四位除数_3_c0 , \四位除数_4_c0 , \四位除数_5_c0 , \四位除数_6_c0 ;
  wire [3:1] \四位除数_8_c0 ;

  // Probe on in_2
  // Probe on in_1
  \四位除数  \u_四位除数_1  (.A0(in_1[7:4]), .B0(in_2), .C0(\四位除数_1_c0 ));  // open: D
  // Probe on \四位除数_1_c0 
  \四位除数  \u_四位除数_2  (.A0({\四位除数_1_c0 , in_1[3]}), .B0(in_2), .C0(\四位除数_2_c0 ));  // open: D
  // Probe on \四位除数_2_c0 
  \四位除数  \u_四位除数_3  (.A0({\四位除数_8_c0 , 1'b0}), .B0(in_2), .C0(\四位除数_3_c0 ));  // open: D
  \四位除数  \u_四位除数_4  (.A0({\四位除数_2_c0 , in_1[2]}), .B0(in_2), .C0(\四位除数_4_c0 ));  // open: D
  // Probe on \四位除数_4_c0 
  \四位除数  \u_四位除数_5  (.A0({\四位除数_3_c0 , 1'b0}), .B0(in_2), .C0(\四位除数_5_c0 ));  // open: D
  \四位除数  \u_四位除数_6  (.A0({\四位除数_4_c0 , in_1[1]}), .B0(in_2), .C0(\四位除数_6_c0 ));  // open: D
  // Probe on \四位除数_6_c0 
  \四位除数  \u_四位除数_7  (.A0({\四位除数_5_c0 , 1'b0}), .B0(in_2), .C0(out_3[2:0]));  // open: D
  \四位除数  \u_四位除数_8  (.A0({\四位除数_6_c0 , in_1[0]}), .B0(in_2), .C0(\四位除数_8_c0 ));  // open: D

  assign out_3[10:3] = in_1;
endmodule

module \四位除数  (
  input  [3:0] A0,
  input  [3:0] B0,
  output [2:0] C0,
  output D
);

  wire [3:0] xor_4_out;
  wire [3:3] multiplexer_1_out;

  // Probe on A0
  // Probe on B0
  xor xor_1 (xor_4_out[3], A0[3], B0[3]);
  xor xor_2 (xor_4_out[2], A0[2], B0[2]);
  xor xor_3 (xor_4_out[1], A0[1], B0[1]);
  xor xor_4 (xor_4_out[0], A0[0], B0[0]);
  Multiplexer #(.width(4)) multiplexer_1 (
    .in0(A0), .in1(xor_4_out), .out({multiplexer_1_out[3], C0}), .sel(A0[3]));  // open: en
  // Probe on {multiplexer_1_out[3], C0}

  assign D = A0[3];

  // Other names for the same wires on the sheet: 被除数[3:0] = A0
endmodule
