// Logisim project dhf p0Q0_FSM.circ as structural Verilog: 4 circuits, main circuit fsm
module fsm (
  input  CLR,
  input  [1:0] In,
  output out_3
);

  wire clk, now1, now2, now3, now4, reset_1_out_2, reset_2_out_2, reset_3_out_2, reset_4_out_2, xin1, xin2,
       xin3, xin4;

  Clock u_CLK (.out(clk));
  reset reset_1 (.state(now4), .out_2(reset_1_out_2));
  reset reset_2 (.state(now3), .out_2(reset_2_out_2));
  reset reset_3 (.state(now2), .out_2(reset_3_out_2));
  reset reset_4 (.state(now1), .out_2(reset_4_out_2));
  trans trans_1 (
    .s4(reset_1_out_2), .s3(reset_2_out_2), .s2(reset_3_out_2), .s1(reset_4_out_2), .In1(In[1]), .In0(In[0]),
    .N4(xin4), .N3(xin3), .N2(xin2), .N1(xin1));  // open: Out
  rgt rgt_1 (.in_1(xin4), .clk(clk), .rst(CLR), .out_4(now4));
  rgt rgt_2 (.in_1(xin3), .clk(clk), .rst(CLR), .out_4(now3));
  rgt rgt_3 (.in_1(xin2), .clk(clk), .rst(CLR), .out_4(now2));
  rgt rgt_4 (.in_1(xin1), .clk(clk), .rst(CLR), .out_4(now1));
  trans trans_2 (
    .s4(now4), .s3(now3), .s2(now2), .s1(now1), .In1(In[1]), .In0(In[0]), .Out(out_3));  // open: N4, N3, N2, N1

  // Other names for the same wires on the sheet: I0 = In[0]; I1 = In[1]; rst = CLR; Z = out_3

  // Notes on the sheet:
  //   端口定义
  //   状态转移
  //   状态存储
  //   输出
endmodule

module trans (
  input  s4,
  input  s3,
  input  s2,
  input  s1,
  input  In1,
  input  In0,
  output N4,
  output N3,
  output N2,
  output N1,
  output Out
);

  wire and_1_out, and_2_out, and_3_out, and_4_out, and_5_out, and_6_out, and_7_out, and_8_out, and_9_out,
       and_10_out, not_1_out, not_2_out, not_3_out, not_4_out, not_5_out, not_6_out, not_7_out, not_8_out,
       not_9_out, not_10_out, not_11_out, not_12_out, not_13_out, not_14_out, not_15_out, not_16_out,
       not_17_out, not_18_out, not_19_out, not_20_out, not_21_out, not_22_out, not_23_out, not_24_out,
       not_25_out, not_26_out, not_27_out, not_28_out, not_29_out, not_30_out, not_31_out, not_32_out,
       not_33_out, not_34_out, not_35_out, not_36_out, not_37_out, not_38_out, not_39_out, not_40_out,
       not_41_out, not_42_out;

  not not_1 (not_1_out, s4);
  not not_2 (not_2_out, s3);
  not not_3 (not_3_out, s2);
  not not_4 (not_4_out, In0);
  not not_5 (not_5_out, s4);
  not not_6 (not_6_out, s3);
  not not_7 (not_7_out, s1);
  not not_8 (not_8_out, In0);
  not not_9 (not_9_out, s4);
  not not_10 (not_10_out, s3);
  not not_11 (not_11_out, s2);
  not not_12 (not_12_out, In1);
  not not_13 (not_13_out, In0);
  not not_14 (not_14_out, s4);
  not not_15 (not_15_out, s3);
  not not_16 (not_16_out, s1);
  not not_17 (not_17_out, In1);
  not not_18 (not_18_out, In0);
  not not_19 (not_19_out, s4);
  not not_20 (not_20_out, s3);
  not not_21 (not_21_out, s2);
  not not_22 (not_22_out, In1);
  not not_23 (not_23_out, s4);
  not not_24 (not_24_out, s3);
  not not_25 (not_25_out, s1);
  not not_26 (not_26_out, In1);
  not not_27 (not_27_out, s4);
  not not_28 (not_28_out, s2);
  not not_29 (not_29_out, s1);
  not not_30 (not_30_out, In1);
  not not_31 (not_31_out, s3);
  not not_32 (not_32_out, s2);
  not not_33 (not_33_out, s1);
  not not_34 (not_34_out, In1);
  not not_35 (not_35_out, s4);
  not not_36 (not_36_out, s2);
  not not_37 (not_37_out, s1);
  not not_38 (not_38_out, In0);
  not not_39 (not_39_out, s3);
  not not_40 (not_40_out, s2);
  not not_41 (not_41_out, s1);
  not not_42 (not_42_out, In0);
  and and_1 (and_1_out, not_1_out, not_2_out, not_3_out, s1, In1, not_4_out);
  and and_2 (and_2_out, not_5_out, not_6_out, s2, not_7_out, In1, not_8_out);
  and and_3 (and_3_out, not_9_out, not_10_out, not_11_out, s1, not_12_out, not_13_out);
  and and_4 (and_4_out, not_14_out, not_15_out, s2, not_16_out, not_17_out, not_18_out);
  and and_5 (and_5_out, not_19_out, not_20_out, not_21_out, s1, not_22_out, In0);
  and and_6 (and_6_out, not_23_out, not_24_out, s2, not_25_out, not_26_out, In0);
  and and_7 (and_7_out, not_27_out, not_28_out, not_29_out, not_30_out, In0);
  and and_8 (and_8_out, not_31_out, not_32_out, not_33_out, not_34_out, In0);
  and and_9 (and_9_out, not_35_out, s3, not_36_out, not_37_out, not_38_out);
  and and_10 (and_10_out, s4, not_39_out, not_40_out, not_41_out, not_42_out);
  or or_1 (N4, and_1_out, and_2_out);
  or or_2 (N3, and_3_out, and_4_out);
  or or_3 (N2, and_5_out, and_6_out);
  or or_4 (N1, and_7_out, and_8_out);
  or or_5 (Out, and_9_out, and_10_out);
endmodule

module reset (
  input  state,
  output out_2
);

  wire clock_1_out, counter_1_q;

  Clock clock_1 (.out(clock_1_out));
  Multiplexer multiplexer_1 (.in0(1'b0), .in1(state), .out(out_2), .sel(counter_1_q));  // open: en
  Counter #(.width(1), .max('h1), .ongoal("stay")) counter_1 (
    .Q(counter_1_q), .clk(clock_1_out));  // open: load, D, count, carry, clr
endmodule

module rgt (
  input  in_1,
  input  clk,
  input  rst,
  output out_4
);

  wire multiplexer_1_out;

  Multiplexer multiplexer_1 (.in0(in_1), .in1(1'b0), .out(multiplexer_1_out), .sel(rst));  // open: en
  Register #(.width(1)) register_1 (.D(multiplexer_1_out), .Q(out_4), .clk(clk));  // open: en, clr
endmodule
