// Logisim project dhfaginfalbe.circ as structural Verilog: 1 circuit, main circuit main
module main (
  input  [2:0] in_1,
  output [3:0] out_2
);

  wire clk, clock_2_out, freeze, not_1_out, set;
  wire [3:0] adder_2_out, ans, multiplexer_1_out, register_2_q;
  wire [7:0] adder_1_out, bit_extender_1_out, counter_1_q;

  Clock clock_1 (.out(clk));
  Counter counter_1 (.Q(counter_1_q), .clk(clock_2_out));  // open: load, D, count, carry, clr
  Clock clock_2 (.out(clock_2_out));
  Counter #(.width(1), .max('h1), .ongoal("stay")) counter_2 (.Q(set), .clk(clk));  // open: load, D, count, carry, clr
  Multiplexer #(.width(4)) multiplexer_1 (
    .in0(4'b0001), .in1(register_2_q), .out(multiplexer_1_out), .sel(set));  // open: en
  Adder adder_1 (.a(counter_1_q), .b(8'h1), .out(adder_1_out));  // open: cin, cout
  assign bit_extender_1_out = {{5{1'b0}}, in_1};  // Bit_Extender bit_extender_1
  Register #(.width(4)) register_1 (.D(multiplexer_1_out), .en(not_1_out), .Q(ans), .clk(clk));  // open: clr
  Adder #(.width(4)) adder_2 (.a(multiplexer_1_out), .b(ans), .out(adder_2_out));  // open: cin, cout
  not not_1 (not_1_out, freeze);
  Comparator #(.mode("unsigned")) comparator_1 (.a(adder_1_out), .b(bit_extender_1_out), .gt(freeze));  // open: eq, lt
  Register #(.width(4)) register_2 (.D(adder_2_out), .en(not_1_out), .Q(register_2_q), .clk(clk));  // open: clr
  Multiplexer #(.width(4)) multiplexer_2 (.in0(4'b0000), .in1(ans), .out(out_2), .sel(freeze));  // open: en

  // Notes on the sheet:
  //   Fn-1
  //   Fn-1
  //   Fn-1
  //   Fn-2
  //   Fn
endmodule
