// Logisim project p0fsm.circ as structural Verilog: 2 circuits, main circuit fsm
// p0FSM
module fsm (
  input  [1:0] in_1,
  input  CLR,
  output Z
);

  wire and_1_out, and_2_out, CLK_out, nor_1_out, not_1_out, not_2_out, or_1_out;
  wire [1:0] multiplexer_1_out, register_1_q, \状态转移_1_s0_ ;

  not not_1 (not_1_out, in_1[1]);
  nor nor_1 (nor_1_out, in_1[0], in_1[1]);
  not not_2 (not_2_out, in_1[0]);
  and and_1 (and_1_out, not_2_out, in_1[1]);
  and and_2 (and_2_out, in_1[0], not_1_out);
  or or_1 (or_1_out, nor_1_out, and_1_out);
  \状态转移  \u_状态转移_1  (
    .S1(register_1_q[1]), .S0(register_1_q[0]), .B(and_2_out), .AC(or_1_out), .S1_(\状态转移_1_s0_ [1]),
    .S0_(\状态转移_1_s0_ [0]), .F(Z));
  Register #(.width(2)) register_1 (.D(multiplexer_1_out), .Q(register_1_q), .clk(CLK_out));  // open: en, clr
  Multiplexer #(.width(2)) multiplexer_1 (
    .in0(\状态转移_1_s0_ ), .in1(2'b00), .out(multiplexer_1_out), .sel(CLR));  // open: en
  Clock CLK (.out(CLK_out));
endmodule

module \状态转移  (
  input  S1,
  input  S0,
  input  B,
  input  AC,
  output S1_,
  output S0_,
  output F
);

  wire and_1_out, and_2_out, and_3_out, and_4_out, and_5_out, and_6_out, not_1_out, not_2_out, not_3_out,
       not_4_out, not_5_out, not_6_out, not_7_out;

  not not_1 (not_1_out, S1);
  and and_1 (and_1_out, not_1_out, S0, AC);
  not not_2 (not_2_out, S1);
  and and_2 (and_2_out, not_2_out, S0, B);
  not not_3 (not_3_out, S0);
  and and_3 (and_3_out, S1, not_3_out, AC);
  not not_4 (not_4_out, S1);
  and and_4 (and_4_out, not_4_out, not_5_out, B);
  not not_5 (not_5_out, S0);
  not not_6 (not_6_out, S1);
  and and_5 (and_5_out, not_6_out, S0, AC);
  and and_6 (and_6_out, S1, not_7_out, AC);
  not not_7 (not_7_out, S0);
  and and_7 (F, S1, S0, AC);
  or or_1 (S1_, and_1_out, and_2_out, and_3_out);
  or or_2 (S0_, and_4_out, and_5_out, and_6_out);
endmodule
