// Logisim project p0grf.circ as structural Verilog: 3 circuits, main circuit 8grf
module grf (
  input  clk,
  input  reset,
  input  WE,
  input  [4:0] A1,
  input  [4:0] A2,
  input  [4:0] A3,
  input  [31:0] WD,
  output [31:0] RD1,
  output [31:0] RD2
);

  wire demultiplexer_2_out0, demultiplexer_2_out1, demultiplexer_2_out2, demultiplexer_2_out3;
  wire [31:0] aa_1_rd1, aa_1_rd2, demultiplexer_1_out0, demultiplexer_1_out1, demultiplexer_1_out2,
       demultiplexer_1_out3, n8grf_1_rd1, n8grf_1_rd2, n8grf_2_rd1, n8grf_2_rd2, n8grf_3_rd1, n8grf_3_rd2;

  Demultiplexer #(.select(2), .width(32)) demultiplexer_1 (
    .out0(demultiplexer_1_out0), .out1(demultiplexer_1_out1), .out2(demultiplexer_1_out2),
    .out3(demultiplexer_1_out3), .in(WD), .sel(A3[4:3]));  // open: en
  aa aa_1 (
    .clk(clk), .reset(reset), .WE(demultiplexer_2_out0), .A1(A1[2:0]), .A2(A2[2:0]), .A3(A3[2:0]),
    .WD(demultiplexer_1_out0), .RD1(aa_1_rd1), .RD2(aa_1_rd2));
  Demultiplexer #(.select(2)) demultiplexer_2 (
    .out0(demultiplexer_2_out0), .out1(demultiplexer_2_out1), .out2(demultiplexer_2_out2),
    .out3(demultiplexer_2_out3), .in(WE), .sel(A3[4:3]));  // open: en
  _8grf u_8grf_1 (
    .clk(clk), .reset(reset), .WE(demultiplexer_2_out2), .A1(A1[2:0]), .A2(A2[2:0]), .A3(A3[2:0]),
    .WD(demultiplexer_1_out2), .RD1(n8grf_1_rd1), .RD2(n8grf_1_rd2));
  _8grf u_8grf_2 (
    .clk(clk), .reset(reset), .WE(demultiplexer_2_out1), .A1(A1[2:0]), .A2(A2[2:0]), .A3(A3[2:0]),
    .WD(demultiplexer_1_out1), .RD1(n8grf_2_rd1), .RD2(n8grf_2_rd2));
  _8grf u_8grf_3 (
    .clk(clk), .reset(reset), .WE(demultiplexer_2_out3), .A1(A1[2:0]), .A2(A2[2:0]), .A3(A3[2:0]),
    .WD(demultiplexer_1_out3), .RD1(n8grf_3_rd1), .RD2(n8grf_3_rd2));
  Multiplexer #(.select(2), .width(32)) multiplexer_1 (
    .in0(aa_1_rd1), .in1(n8grf_2_rd1), .in2(n8grf_1_rd1), .in3(n8grf_3_rd1), .out(RD1), .sel(A1[4:3]));  // open: en
  Multiplexer #(.select(2), .width(32)) multiplexer_2 (
    .in0(aa_1_rd2), .in1(n8grf_2_rd2), .in2(n8grf_1_rd2), .in3(n8grf_3_rd2), .out(RD2), .sel(A2[4:3]));  // open: en
endmodule

module _8grf (
  input  clk,
  input  reset,
  input  WE,
  input  [2:0] A1,
  input  [2:0] A2,
  input  [2:0] A3,
  input  [31:0] WD,
  output [31:0] RD1,
  output [31:0] RD2
);

  wire demultiplexer_1_out0, demultiplexer_1_out1, demultiplexer_1_out2, demultiplexer_1_out3,
       demultiplexer_1_out4, demultiplexer_1_out5, demultiplexer_1_out6, demultiplexer_1_out7;
  wire [31:0] demultiplexer_2_out0, demultiplexer_2_out1, demultiplexer_2_out2, demultiplexer_2_out3,
       demultiplexer_2_out4, demultiplexer_2_out5, demultiplexer_2_out6, demultiplexer_2_out7, register_1_q,
       register_2_q, register_3_q, register_4_q, register_5_q, register_6_q, register_7_q, register_8_q;

  Demultiplexer #(.select(3)) demultiplexer_1 (
    .out0(demultiplexer_1_out0), .out1(demultiplexer_1_out1), .out2(demultiplexer_1_out2),
    .out3(demultiplexer_1_out3), .out4(demultiplexer_1_out4), .out5(demultiplexer_1_out5),
    .out6(demultiplexer_1_out6), .out7(demultiplexer_1_out7), .in(WE), .sel(A3));  // open: en
  Register #(.width(32)) register_1 (
    .D(demultiplexer_2_out0), .en(demultiplexer_1_out0), .Q(register_1_q), .clk(clk), .clr(reset));
  Demultiplexer #(.select(3), .width(32)) demultiplexer_2 (
    .out0(demultiplexer_2_out0), .out1(demultiplexer_2_out1), .out2(demultiplexer_2_out2),
    .out3(demultiplexer_2_out3), .out4(demultiplexer_2_out4), .out5(demultiplexer_2_out5),
    .out6(demultiplexer_2_out6), .out7(demultiplexer_2_out7), .in(WD), .sel(A3));  // open: en
  Register #(.width(32)) register_2 (
    .D(demultiplexer_2_out1), .en(demultiplexer_1_out1), .Q(register_2_q), .clk(clk), .clr(reset));
  Register #(.width(32)) register_3 (
    .D(demultiplexer_2_out2), .en(demultiplexer_1_out2), .Q(register_3_q), .clk(clk), .clr(reset));
  Register #(.width(32)) register_4 (
    .D(demultiplexer_2_out4), .en(demultiplexer_1_out4), .Q(register_4_q), .clk(clk), .clr(reset));
  Register #(.width(32)) register_5 (
    .D(demultiplexer_2_out3), .en(demultiplexer_1_out3), .Q(register_5_q), .clk(clk), .clr(reset));
  Register #(.width(32)) register_6 (
    .D(demultiplexer_2_out5), .en(demultiplexer_1_out5), .Q(register_6_q), .clk(clk), .clr(reset));
  Register #(.width(32)) register_7 (
    .D(demultiplexer_2_out6), .en(demultiplexer_1_out6), .Q(register_7_q), .clk(clk), .clr(reset));
  Register #(.width(32)) register_8 (
    .D(demultiplexer_2_out7), .en(demultiplexer_1_out7), .Q(register_8_q), .clk(clk), .clr(reset));
  Multiplexer #(.select(3), .width(32)) multiplexer_1 (
    .in0(register_1_q), .in1(register_2_q), .in2(register_3_q), .in3(register_5_q), .in4(register_4_q),
    .in5(register_6_q), .in6(register_7_q), .in7(register_8_q), .out(RD1), .sel(A1));  // open: en
  Multiplexer #(.select(3), .width(32)) multiplexer_2 (
    .in0(register_1_q), .in1(register_2_q), .in2(register_3_q), .in3(register_5_q), .in4(register_4_q),
    .in5(register_6_q), .in6(register_7_q), .in7(register_8_q), .out(RD2), .sel(A2));  // open: en
endmodule

module aa (
  input  clk,
  input  reset,
  input  WE,
  input  [2:0] A1,
  input  [2:0] A2,
  input  [2:0] A3,
  input  [31:0] WD,
  output [31:0] RD1,
  output [31:0] RD2
);

  wire demultiplexer_1_out1, demultiplexer_1_out2, demultiplexer_1_out3, demultiplexer_1_out4,
       demultiplexer_1_out5, demultiplexer_1_out6, demultiplexer_1_out7, undriven;
  wire [31:0] demultiplexer_2_out1, demultiplexer_2_out2, demultiplexer_2_out3, demultiplexer_2_out4,
       demultiplexer_2_out5, demultiplexer_2_out6, demultiplexer_2_out7, register_1_q, register_2_q,
       register_3_q, register_4_q, register_5_q, register_6_q, register_7_q, register_8_q;

  Demultiplexer #(.select(3)) demultiplexer_1 (
    .out1(demultiplexer_1_out1), .out2(demultiplexer_1_out2), .out3(demultiplexer_1_out3),
    .out4(demultiplexer_1_out4), .out5(demultiplexer_1_out5), .out6(demultiplexer_1_out6),
    .out7(demultiplexer_1_out7), .in(WE), .sel(A3));  // open: out0, en
  Register #(.width(32)) register_1 (
    .D(demultiplexer_2_out1), .en(demultiplexer_1_out1), .Q(register_1_q), .clk(clk), .clr(reset));
  Register #(.width(32)) register_2 (.D({32{1'b0}}), .en(undriven), .Q(register_2_q), .clk(clk), .clr(reset));
  Demultiplexer #(.select(3), .width(32)) demultiplexer_2 (
    .out1(demultiplexer_2_out1), .out2(demultiplexer_2_out2), .out3(demultiplexer_2_out3),
    .out4(demultiplexer_2_out4), .out5(demultiplexer_2_out5), .out6(demultiplexer_2_out6),
    .out7(demultiplexer_2_out7), .in(WD), .sel(A3));  // open: out0, en
  Register #(.width(32)) register_3 (
    .D(demultiplexer_2_out2), .en(demultiplexer_1_out2), .Q(register_3_q), .clk(clk), .clr(reset));
  Register #(.width(32)) register_4 (
    .D(demultiplexer_2_out4), .en(demultiplexer_1_out4), .Q(register_4_q), .clk(clk), .clr(reset));
  Register #(.width(32)) register_5 (
    .D(demultiplexer_2_out3), .en(demultiplexer_1_out3), .Q(register_5_q), .clk(clk), .clr(reset));
  Register #(.width(32)) register_6 (
    .D(demultiplexer_2_out5), .en(demultiplexer_1_out5), .Q(register_6_q), .clk(clk), .clr(reset));
  Register #(.width(32)) register_7 (
    .D(demultiplexer_2_out6), .en(demultiplexer_1_out6), .Q(register_7_q), .clk(clk), .clr(reset));
  Register #(.width(32)) register_8 (
    .D(demultiplexer_2_out7), .en(demultiplexer_1_out7), .Q(register_8_q), .clk(clk), .clr(reset));
  Multiplexer #(.select(3), .width(32)) multiplexer_1 (
    .in0(register_2_q), .in1(register_1_q), .in2(register_3_q), .in3(register_5_q), .in4(register_4_q),
    .in5(register_6_q), .in6(register_7_q), .in7(register_8_q), .out(RD1), .sel(A1));  // open: en
  Multiplexer #(.select(3), .width(32)) multiplexer_2 (
    .in0(register_2_q), .in1(register_1_q), .in2(register_3_q), .in3(register_5_q), .in4(register_4_q),
    .in5(register_6_q), .in6(register_7_q), .in7(register_8_q), .out(RD2), .sel(A2));  // open: en
endmodule
