// Logisim project p0nv.circ as structural Verilog: 3 circuits, main circuit navigation
module navigation (
  input  [1:0] dir,
  input  clk,
  input  reset,
  output arrive,
  output hit
);

  wire and_1_out, not_1_out, \状态转移_1_h ;
  wire [2:0] register_1_q, \状态转移_1_s0_ ;

  \状态输出  \u_状态输出_1  (.in_1(register_1_q[2]), .in_2(register_1_q[1]), .in_3(register_1_q[0]), .out_4(arrive));
  \状态转移  \u_状态转移_1  (
    .S2(register_1_q[2]), .S1(register_1_q[1]), .S0(register_1_q[0]), .I1(dir[1]), .I0(dir[0]),
    .S2_(\状态转移_1_s0_ [2]), .S1_(\状态转移_1_s0_ [1]), .S0_(\状态转移_1_s0_ [0]), .h(\状态转移_1_h ));
  Register #(.width(3)) register_1 (.D(\状态转移_1_s0_ ), .Q(register_1_q), .clk(clk), .clr(reset));  // open: en
  not not_1 (not_1_out, arrive);
  and and_1 (and_1_out, not_1_out, \状态转移_1_h );
  Register #(.width(1)) register_2 (.D(and_1_out), .Q(hit), .clk(clk), .clr(reset));  // open: en
endmodule

module \状态转移  (
  input  S2,
  input  S1,
  input  S0,
  input  I1,
  input  I0,
  output S2_,
  output S1_,
  output S0_,
  output h
);

  wire and_1_out, and_2_out, and_3_out, and_4_out, and_5_out, and_6_out, and_7_out, and_8_out, and_9_out,
       and_10_out, and_11_out, and_12_out, and_13_out, and_14_out, and_15_out, and_16_out, and_17_out,
       and_18_out, and_19_out, and_20_out, and_21_out, and_22_out, and_23_out, not_1_out, not_2_out,
       not_3_out, not_4_out, not_5_out, not_6_out, not_7_out, not_8_out, not_9_out, not_10_out, not_11_out,
       not_12_out, not_13_out, not_14_out, not_15_out, not_16_out, not_17_out, not_18_out, not_19_out,
       not_20_out, not_21_out, not_22_out, not_23_out, not_24_out, not_25_out, not_26_out, not_27_out,
       not_28_out, not_29_out, not_30_out, not_31_out, not_32_out, not_33_out, not_34_out, not_35_out,
       not_36_out, not_37_out, not_38_out;

  not not_1 (not_1_out, S0);
  not not_2 (not_2_out, I1);
  not not_3 (not_3_out, I1);
  not not_4 (not_4_out, I0);
  not not_5 (not_5_out, S1);
  not not_6 (not_6_out, I0);
  not not_7 (not_7_out, S1);
  not not_8 (not_8_out, I1);
  not not_9 (not_9_out, I1);
  not not_10 (not_10_out, S0);
  not not_11 (not_11_out, I1);
  not not_12 (not_12_out, I0);
  not not_13 (not_13_out, S0);
  not not_14 (not_14_out, I0);
  not not_15 (not_15_out, S1);
  not not_16 (not_16_out, I0);
  not not_17 (not_17_out, S2);
  not not_18 (not_18_out, S1);
  not not_19 (not_19_out, S0);
  not not_20 (not_20_out, I1);
  not not_21 (not_21_out, I0);
  not not_22 (not_22_out, I0);
  not not_23 (not_23_out, S2);
  not not_24 (not_24_out, S1);
  not not_25 (not_25_out, S0);
  not not_26 (not_26_out, S2);
  not not_27 (not_27_out, S1);
  not not_28 (not_28_out, S0);
  not not_29 (not_29_out, S2);
  not not_30 (not_30_out, S1);
  not not_31 (not_31_out, S2);
  not not_32 (not_32_out, S0);
  not not_33 (not_33_out, S0);
  not not_34 (not_34_out, I1);
  not not_35 (not_35_out, I0);
  not not_36 (not_36_out, I1);
  not not_37 (not_37_out, I0);
  not not_38 (not_38_out, I0);
  and and_1 (and_1_out, S1, not_1_out, not_2_out, I0);
  and and_2 (and_2_out, S1, S0, not_3_out, not_4_out);
  and and_3 (and_3_out, S2, not_5_out, S0, I1, not_6_out);
  and and_4 (and_4_out, S2, S1, S0, I1, I0);
  and and_5 (and_5_out, not_7_out, S0, not_8_out);
  and and_6 (and_6_out, S0, not_9_out, I0);
  and and_7 (and_7_out, S1, not_10_out, not_11_out, not_12_out);
  and and_8 (and_8_out, S1, not_13_out, I1, I0);
  and and_9 (and_9_out, S1, S0, I1, not_14_out);
  and and_10 (and_10_out, S2, not_15_out, S0, not_16_out);
  and and_11 (and_11_out, not_17_out, not_18_out, not_19_out, not_20_out, not_21_out);
  and and_12 (and_12_out, S0, I0);
  and and_13 (and_13_out, S1, I1, not_22_out);
  and and_14 (and_14_out, S2, S0, I1);
  and and_15 (and_15_out, not_23_out, not_24_out, not_25_out, I0);
  and and_16 (and_16_out, not_26_out, not_27_out, not_28_out, I1);
  and and_17 (and_17_out, not_29_out, not_30_out, I1, I0);
  and and_18 (and_18_out, not_31_out, not_32_out, I1, I0);
  and and_19 (and_19_out, S1, not_33_out, not_34_out, not_35_out);
  and and_20 (and_20_out, S1, S0, not_36_out, I0);
  and and_21 (and_21_out, S1, S0, I1, not_37_out);
  and and_22 (and_22_out, S2, S0, I1, not_38_out);
  and and_23 (and_23_out, S2, S1, S0, I1);
  or or_1 (S2_, and_1_out, and_2_out, and_3_out, and_4_out);
  or or_2 (S1_, and_5_out, and_6_out, and_7_out, and_8_out, and_9_out, and_10_out);
  or or_3 (S0_, and_11_out, and_12_out, and_13_out, and_14_out);
  or or_4 (h, and_15_out, and_16_out, and_17_out, and_18_out, and_19_out, and_20_out, and_21_out, and_22_out, and_23_out);
endmodule

module \状态输出  (
  input  in_1,
  input  in_2,
  input  in_3,
  output out_4
);

  wire not_1_out, not_2_out;

  not not_1 (not_1_out, in_3);
  not not_2 (not_2_out, in_2);
  and and_1 (out_4, in_1, not_2_out, not_1_out);
endmodule
