// Logisim project ss.circ as structural Verilog: 1 circuit, main circuit CRC
module CRC (
  input  [7:0] in_1,
  input  [3:0] in_2,
  output [11:0] out_3
);


  assign out_3 = {in_1, in_2};
endmodule
