// Logisim project 元件总结.circ as structural Verilog: 1 circuit, main circuit main
module main (
  input  in_1,
  input  \输入_出 ,
  input  [7:0] \位数扩展器 ,
  input  [1:0] in_4,
  input  \使能端en ,
  input  load,
  input  [2:0] data,
  input  count,
  input  \_1bits_输入 ,
  output [15:0] out_10,
  output out_11,
  output out_12,
  output out_13,
  output out_14,
  output \寄存器 ,
  output [2:0] \清零重置rst__1 ,
  output out_17,
  output \输出_nQ 
);

  wire clock_1_out, clock_2_out, clock_3_out;

  Clock clock_1 (.out(clock_1_out));
  assign out_10 = {{8{in_1}}, \位数扩展器 };  // Bit_Extender bit_extender_1
  Multiplexer #(.disabled(0)) multiplexer_1 ();  // open: in0, in1, out, sel, en
  Comparator comparator_1 ();  // open: a, b, gt, eq, lt
  D_Flip_Flop d_ff_1 (.clk(clock_1_out), .D(\_1bits_输入 ), .Q(out_17), .Qn(\输出_nQ ));  // open: preset, en, reset
  Demultiplexer demultiplexer_1 ();  // open: out0, out1, in, sel, en
  Register #(.width(1)) register_1 (.D(\使能端en ), .Q(\寄存器 ), .clk(clock_2_out));  // open: en, clr
  Clock clock_2 (.out(clock_2_out));
  Clock clock_3 (.out(clock_3_out));
  Decoder #(.tristate("true"), .disabled(0)) decoder_1 ();  // open: out0, out1, sel, en
  Counter #(.width(3), .max('h5), .ongoal("load")) counter_1 (
    .load(load), .D(data), .count(count), .Q(\清零重置rst__1 ), .clk(clock_3_out));  // open: carry, clr
  Decoder #(.select(2), .disabled(0)) decoder_2 (
    .out0(out_11), .out1(out_12), .out2(out_13), .out3(out_14), .sel(in_4));  // open: en

  // Notes on the sheet:
  //   使能端en
  //   sel==0时，输出
  //   sel==1时，输出
  //   选择端sel
  //   a
  //   b
  //   trigger选edge
  //   clk/电平
  //   优先清零重置prst
  //   使能端en冻结clk
  //   多路选择器
  //   使能端en
  //   比较器
  //   a大于b时输出1
  //   注意：数据类型是选有符号还是无符号
  //   trigger选level
  //   D触发器/锁存器
  //   时钟端clk，上升沿时/电平型高电平时更新触发器值为D
  //   清零重置rst==1
  //   Extension type可设置位数扩展类型（0、1、有符号位、input端口1bit）
  //   输出Q(触发器所存值)
  //   多路分配器
  //   选择端sel
  //   en==1(或未连接）时输出1，该元件正常工作，en==0时可设置输出floating浮动值/zero0，该元件被冻结，不工作
  //   分位器
  //   应用：做移位器
  //   sel==0时，输出
  //   sel==1时，输出
  //   使能端en
  //   时钟端clk，上升沿时更新寄存器值为D
  //   load==1&&count==0&&clk上升沿时
  //   计数器输出data的值并保持
  //   注意：选floating浮动状态时啥也连接不上
  //   输出寄存器的值
  //   reset==1时，清零重置
  //   load==1&&count==1 计数器值递减
  //   load==0&&count==0 计数器不计数
  //   使能端en
  //   注意：异步复位
  //   计数器
  //   Three-state:未输入时的端口输出float(x)还是zero(0)
  //   PullBehavior:据说可以实现加法器的进位输入
  //   译码器
  //   应用：将二进制编码转换成独热码
  //   Three-state:sel未选择的端口输出float(x)还是zero(0)
  //   Stay:保持最值
  //   Load:载入data的值
  //   选择端sel决定哪个端口输出1
  //   Action On Overflow
  //   计数器达最值时
  //   Wrap:回到0/最大值，周期循环
  //   Continue:在bits范围内继续变化
endmodule
