// Logisim project 斐波那契.circ as structural Verilog: 3 circuits, main circuit main
module main (
  input  [2:0] N,
  output [3:0] Nth
);

  wire counter_1_out_3, undriven;
  wire [3:0] compute_1_out_2;
  wire [7:0] bit_extender_1_out;

  assign bit_extender_1_out = {{5{1'b0}}, N};  // Bit_Extender bit_extender_1
  Clock clock_1 ();  // open: out
  counter counter_1 (.in_1(bit_extender_1_out), .in_2(undriven), .out_3(counter_1_out_3));
  compute compute_1 (.in_1(undriven), .out_2(compute_1_out_2));
  Register #(.width(4)) register_1 (.D(compute_1_out_2), .Q(Nth), .clk(counter_1_out_3), .clr(undriven));  // open: en
endmodule

module counter (
  input  [7:0] in_1,
  input  in_2,
  output out_3
);

  wire clock_1_out;
  wire [7:0] adder_1_out, register_1_q;

  Clock clock_1 (.out(clock_1_out));
  Register register_1 (.D(adder_1_out), .Q(register_1_q), .clk(clock_1_out), .clr(in_2));  // open: en
  Adder adder_1 (.a(register_1_q), .b(8'h1), .out(adder_1_out));  // open: cin, cout
  // Probe on adder_1_out
  Comparator #(.mode("unsigned")) comparator_1 (.a(adder_1_out), .b(in_1), .gt(out_3));  // open: eq, lt

  // Other names for the same wires on the sheet: clear = in_2
endmodule

module compute (
  input  in_1,
  output [3:0] out_2
);

  wire clock_1_out, d_ff_1_q;
  wire [3:0] adder_1_out, multiplexer_1_out, previos_q;

  Clock clock_1 (.out(clock_1_out));
  Multiplexer #(.width(4)) multiplexer_1 (
    .in0(4'b0001), .in1(adder_1_out), .out(multiplexer_1_out), .sel(d_ff_1_q));  // open: en
  D_Flip_Flop d_ff_1 (.clk(clock_1_out), .D(1'b1), .Q(d_ff_1_q), .reset(in_1));  // open: Qn, preset, en
  // Probe on out_2
  // Probe on out_2
  Register #(.width(4)) now (.D(multiplexer_1_out), .Q(out_2), .clk(clock_1_out), .clr(in_1));  // open: en
  Register #(.width(4)) previos (.D(out_2), .Q(previos_q), .clk(clock_1_out), .clr(in_1));  // open: en
  Adder #(.width(4)) adder_1 (.a(out_2), .b(previos_q), .out(adder_1_out));  // open: cin, cout

  // Other names for the same wires on the sheet: clear = in_1
endmodule
