// Logisim project P3testwithjr.circ as structural Verilog: 9 circuits, main circuit GRF
module main (
  input  in_1,
  output [31:0] out_2,
  output out_3,
  output [4:0] out_4,
  output [31:0] out_5,
  output out_6,
  output [4:0] out_7,
  output [31:0] out_8
);

  wire alu_1_zero, and_1_out, clock_1_out, control_1_alusrc, control_1_memtoreg, control_1_need_aluc,
       control_1_need_j, control_1_npc_sel, control_1_regdst, need_pctora, or_1_out;
  wire [1:0] alucontrol_1_aluop, control_1_aluop, control_1_extop, multiplexer_5_out;
  wire [4:0] instruction_memory_1_rd, instruction_memory_1_rs, instruction_memory_1_rt, multiplexer_1_out;
  wire [5:0] instruction_memory_1_funct, instruction_memory_1_op;
  wire [15:0] instruction_memory_1_imm;
  wire [25:0] instruction_memory_1_instr_index;
  wire [31:0] adder_1_out, alu_1_out, bit_extender_1_out, data_memory_1_outdata, grf_1_rd1,
       multiplexer_4_out, multiplexer_6_out, multiplexer_7_out, multiplexer_8_out, pc_1_pc_4, pc_1_pcnow,
       shifter_1_out, sign_ext_1_result;

  PC pc_1 (.PCin_next(multiplexer_7_out), .PCnow(pc_1_pcnow), .PC_4(pc_1_pc_4), .CLR(in_1), .CLK(clock_1_out));
  Clock clock_1 (.out(clock_1_out));
  Instruction_Memory instruction_memory_1 (
    .program_counter_address(pc_1_pcnow), .Op(instruction_memory_1_op), .rs(instruction_memory_1_rs),
    .rt(instruction_memory_1_rt), .rd(instruction_memory_1_rd), .funct(instruction_memory_1_funct),
    .imm(instruction_memory_1_imm), .Instr(out_2), .instr_index(instruction_memory_1_instr_index));  // open: shamt
  assign bit_extender_1_out = {{6{1'b0}}, instruction_memory_1_instr_index};  // Bit_Extender bit_extender_1
  Multiplexer #(.width(5)) multiplexer_1 (
    .in0(instruction_memory_1_rt), .in1(instruction_memory_1_rd), .out(multiplexer_1_out),
    .sel(control_1_regdst));  // open: en
  Multiplexer #(.width(5)) multiplexer_2 (
    .in0(multiplexer_1_out), .in1({5{1'b1}}), .out(out_4), .sel(need_pctora));  // open: en
  Multiplexer #(.width(32)) multiplexer_3 (
    .in0(multiplexer_8_out), .in1(pc_1_pc_4), .sel(need_pctora));  // open: out, en
  GRF grf_1 (
    .CLK(clock_1_out), .CLR(in_1), .A1(instruction_memory_1_rs), .A2(instruction_memory_1_rt), .A3(out_4),
    .WD(out_5), .WE(out_3), .RD1(grf_1_rd1), .RD2(out_8));
  ALUControl alucontrol_1 (.func(instruction_memory_1_funct), .ALUOp(alucontrol_1_aluop));
  Control control_1 (
    .op(instruction_memory_1_op), .RegDst(control_1_regdst), .ALUSrc(control_1_alusrc),
    .MemtoReg(control_1_memtoreg), .Regwrite(out_3), .MemWrite(out_6), .nPC_sel(control_1_npc_sel),
    .ExtOp(control_1_extop), .ALUOp(control_1_aluop), .need_ALUC(control_1_need_aluc),
    .need_j(control_1_need_j), .need__pc_to_ra(need_pctora));
  sign_EXT sign_ext_1 (.immin(instruction_memory_1_imm), .EXTOp(control_1_extop), .Result(sign_ext_1_result));
  // Probe on out_2
  // Probe on out_4
  // Probe on out_7
  // Probe on out_8
  Multiplexer #(.width(32)) multiplexer_4 (
    .in0(out_8), .in1(sign_ext_1_result), .out(multiplexer_4_out), .sel(control_1_alusrc));  // open: en
  // Probe on out_5
  ALU alu_1 (.A(grf_1_rd1), .B(multiplexer_4_out), .out(alu_1_out), .zero(alu_1_zero), .ALUOp(multiplexer_5_out));
  Multiplexer #(.width(2)) multiplexer_5 (
    .in0(control_1_aluop), .in1(alucontrol_1_aluop), .out(multiplexer_5_out), .sel(control_1_need_aluc));  // open: en
  Shifter #(.width(32)) shifter_1 (.in(sign_ext_1_result), .\dist (5'b00010), .out(shifter_1_out));
  Adder #(.width(32)) adder_1 (.a(pc_1_pc_4), .b(shifter_1_out), .out(adder_1_out));  // open: cin, cout
  // Probe on nothing
  Multiplexer #(.width(32)) multiplexer_6 (
    .in0(adder_1_out), .in1(bit_extender_1_out), .out(multiplexer_6_out), .sel(control_1_need_j));  // open: en
  and and_1 (and_1_out, control_1_npc_sel, alu_1_zero);
  // Probe on nothing
  Multiplexer #(.width(32)) multiplexer_7 (
    .in0(pc_1_pc_4), .in1(multiplexer_6_out), .out(multiplexer_7_out), .sel(or_1_out));  // open: en
  or or_1 (or_1_out, control_1_need_j, and_1_out);
  Data_Memory data_memory_1 (
    .WData(out_8), .WriteEn(out_6), .CLK(clock_1_out), .CLR(in_1), .outDATA(data_memory_1_outdata),
    .Address(alu_1_out), .MemAddr(out_7));  // open: ReadEn
  Multiplexer #(.width(32)) multiplexer_8 (
    .in0(alu_1_out), .in1(data_memory_1_outdata), .out(multiplexer_8_out), .sel(control_1_memtoreg));  // open: en

  // Other names for the same wires on the sheet: Instr[31:0] = out_2; MemAddr[4:0] = out_7; MemData[31:0] = out_8;
  //   MemWrite = out_6; RegAddr[4:0] = out_4; RegData[31:0] = out_5; RegWrite = out_3; Reset = in_1

  // Notes on the sheet:
  //   this is a output for test
endmodule

module GRF (
  input  CLK,
  input  CLR,
  input  [4:0] A1,
  input  [4:0] A2,
  input  [4:0] A3,
  input  [31:0] WD,
  input  WE,
  output [31:0] RD1,
  output [31:0] RD2
);

  wire [7:0] demultiplexer_1_out0, demultiplexer_1_out8, demultiplexer_1_out16, demultiplexer_1_out24;
  wire [31:0] _1, _2, _3, _4, _5, _6, _7, _8, _9, _10, _11, _12, _13, _14, _15, _16, _17, _18, _19, _20, _21,
       _22, _23, _24, _25, _26, _27, _28, _29, _30, _31, I0, I1, I2, I3, I4, I5, I6, I7, I8, I9, I10, I11,
       I12, I13, I14, I15, I16, I17, I18, I19, I20, I21, I22, I23, I24, I25, I26, I27, I28, I29, I30, I31;

  // Probe on {32{1'b0}}
  // Probe on _1
  // Probe on _2
  // Probe on _3
  // Probe on _4
  // Probe on _5
  // Probe on _6
  // Probe on _7
  // Probe on _8
  // Probe on _9
  // Probe on _10
  // Probe on _11
  // Probe on _12
  // Probe on _13
  // Probe on _14
  // Probe on _15
  // Probe on _16
  // Probe on _17
  // Probe on _18
  // Probe on _19
  // Probe on _20
  // Probe on _21
  // Probe on _22
  // Probe on _23
  // Probe on _24
  // Probe on _25
  // Probe on _26
  // Probe on _27
  // Probe on _28
  // Probe on _29
  // Probe on _30
  // Probe on _31
  // Probe on A1
  // Probe on A2
  // Probe on A3
  Demultiplexer #(.select(5)) demultiplexer_1 (
    .out0(demultiplexer_1_out0[0]), .out1(demultiplexer_1_out0[1]), .out2(demultiplexer_1_out0[2]),
    .out3(demultiplexer_1_out0[3]), .out4(demultiplexer_1_out0[4]), .out5(demultiplexer_1_out0[5]),
    .out6(demultiplexer_1_out0[6]), .out7(demultiplexer_1_out0[7]), .out8(demultiplexer_1_out8[0]),
    .out9(demultiplexer_1_out8[1]), .out10(demultiplexer_1_out8[2]), .out11(demultiplexer_1_out8[3]),
    .out12(demultiplexer_1_out8[4]), .out13(demultiplexer_1_out8[5]), .out14(demultiplexer_1_out8[6]),
    .out15(demultiplexer_1_out8[7]), .out16(demultiplexer_1_out16[0]), .out17(demultiplexer_1_out16[1]),
    .out18(demultiplexer_1_out16[2]), .out19(demultiplexer_1_out16[3]), .out20(demultiplexer_1_out16[4]),
    .out21(demultiplexer_1_out16[5]), .out22(demultiplexer_1_out16[6]), .out23(demultiplexer_1_out16[7]),
    .out24(demultiplexer_1_out24[0]), .out25(demultiplexer_1_out24[1]), .out26(demultiplexer_1_out24[2]),
    .out27(demultiplexer_1_out24[3]), .out28(demultiplexer_1_out24[4]), .out29(demultiplexer_1_out24[5]),
    .out30(demultiplexer_1_out24[6]), .out31(demultiplexer_1_out24[7]), .in(WE), .sel(A3));  // open: en
  Demultiplexer #(.select(5), .width(32)) demultiplexer_2 (
    .out0(I0), .out1(I1), .out2(I2), .out3(I3), .out4(I4), .out5(I5), .out6(I6), .out7(I7), .out8(I8),
    .out9(I9), .out10(I10), .out11(I11), .out12(I12), .out13(I13), .out14(I14), .out15(I15), .out16(I16),
    .out17(I17), .out18(I18), .out19(I19), .out20(I20), .out21(I21), .out22(I22), .out23(I23), .out24(I24),
    .out25(I25), .out26(I26), .out27(I27), .out28(I28), .out29(I29), .out30(I30), .out31(I31), .in(WD),
    .sel(A3));  // open: en
  Register #(.width(32)) register_1 (.D(I8), .en(demultiplexer_1_out8[0]), .Q(_8), .clk(CLK), .clr(CLR));
  Register #(.width(32)) register_2 (.D(I16), .en(demultiplexer_1_out16[0]), .Q(_16), .clk(CLK), .clr(CLR));
  Register #(.width(32)) register_3 (.D(I24), .en(demultiplexer_1_out24[0]), .Q(_24), .clk(CLK), .clr(CLR));
  Register #(.width(32)) register_4 (.D(I1), .en(demultiplexer_1_out0[1]), .Q(_1), .clk(CLK), .clr(CLR));
  Register #(.width(32)) register_5 (.D(I9), .en(demultiplexer_1_out8[1]), .Q(_9), .clk(CLK), .clr(CLR));
  Register #(.width(32)) register_6 (.D(I17), .en(demultiplexer_1_out16[1]), .Q(_17), .clk(CLK), .clr(CLR));
  Register #(.width(32)) register_7 (.D(I25), .en(demultiplexer_1_out24[1]), .Q(_25), .clk(CLK), .clr(CLR));
  Register #(.width(32)) register_8 (.D(I2), .en(demultiplexer_1_out0[2]), .Q(_2), .clk(CLK), .clr(CLR));
  Register #(.width(32)) register_9 (.D(I10), .en(demultiplexer_1_out8[2]), .Q(_10), .clk(CLK), .clr(CLR));
  Register #(.width(32)) register_10 (.D(I18), .en(demultiplexer_1_out16[2]), .Q(_18), .clk(CLK), .clr(CLR));
  Register #(.width(32)) register_11 (.D(I26), .en(demultiplexer_1_out24[2]), .Q(_26), .clk(CLK), .clr(CLR));
  Register #(.width(32)) register_12 (.D(I3), .en(demultiplexer_1_out0[3]), .Q(_3), .clk(CLK), .clr(CLR));
  Register #(.width(32)) register_13 (.D(I11), .en(demultiplexer_1_out8[3]), .Q(_11), .clk(CLK), .clr(CLR));
  Register #(.width(32)) register_14 (.D(I19), .en(demultiplexer_1_out16[3]), .Q(_19), .clk(CLK), .clr(CLR));
  Register #(.width(32)) register_15 (.D(I27), .en(demultiplexer_1_out24[3]), .Q(_27), .clk(CLK), .clr(CLR));
  Register #(.width(32)) register_16 (.D(I4), .en(demultiplexer_1_out0[4]), .Q(_4), .clk(CLK), .clr(CLR));
  Register #(.width(32)) register_17 (.D(I12), .en(demultiplexer_1_out8[4]), .Q(_12), .clk(CLK), .clr(CLR));
  Register #(.width(32)) register_18 (.D(I20), .en(demultiplexer_1_out16[4]), .Q(_20), .clk(CLK), .clr(CLR));
  Register #(.width(32)) register_19 (.D(I28), .en(demultiplexer_1_out24[4]), .Q(_28), .clk(CLK), .clr(CLR));
  Register #(.width(32)) register_20 (.D(I5), .en(demultiplexer_1_out0[5]), .Q(_5), .clk(CLK), .clr(CLR));
  Register #(.width(32)) register_21 (.D(I13), .en(demultiplexer_1_out8[5]), .Q(_13), .clk(CLK), .clr(CLR));
  Register #(.width(32)) register_22 (.D(I21), .en(demultiplexer_1_out16[5]), .Q(_21), .clk(CLK), .clr(CLR));
  Register #(.width(32)) register_23 (.D(I29), .en(demultiplexer_1_out24[5]), .Q(_29), .clk(CLK), .clr(CLR));
  Register #(.width(32)) register_24 (.D(I6), .en(demultiplexer_1_out0[6]), .Q(_6), .clk(CLK), .clr(CLR));
  Register #(.width(32)) register_25 (.D(I14), .en(demultiplexer_1_out8[6]), .Q(_14), .clk(CLK), .clr(CLR));
  Register #(.width(32)) register_26 (.D(I22), .en(demultiplexer_1_out16[6]), .Q(_22), .clk(CLK), .clr(CLR));
  Register #(.width(32)) register_27 (.D(I30), .en(demultiplexer_1_out24[6]), .Q(_30), .clk(CLK), .clr(CLR));
  Register #(.width(32)) register_28 (.D(I7), .en(demultiplexer_1_out0[7]), .Q(_7), .clk(CLK), .clr(CLR));
  Register #(.width(32)) register_29 (.D(I15), .en(demultiplexer_1_out8[7]), .Q(_15), .clk(CLK), .clr(CLR));
  Register #(.width(32)) register_30 (.D(I23), .en(demultiplexer_1_out16[7]), .Q(_23), .clk(CLK), .clr(CLR));
  Register #(.width(32)) register_31 (.D(I31), .en(demultiplexer_1_out24[7]), .Q(_31), .clk(CLK), .clr(CLR));
  Multiplexer #(.select(5), .width(32)) multiplexer_1 (
    .in0({32{1'b0}}), .in1(_1), .in2(_2), .in3(_3), .in4(_4), .in5(_5), .in6(_6), .in7(_7), .in8(_8),
    .in9(_9), .in10(_10), .in11(_11), .in12(_12), .in13(_13), .in14(_14), .in15(_15), .in16(_16), .in17(_17),
    .in18(_18), .in19(_19), .in20(_20), .in21(_21), .in22(_22), .in23(_23), .in24(_24), .in25(_25),
    .in26(_26), .in27(_27), .in28(_28), .in29(_29), .in30(_30), .in31(_31), .out(RD1), .sel(A1));  // open: en
  Multiplexer #(.select(5), .width(32)) multiplexer_2 (
    .in0({32{1'b0}}), .in1(_1), .in2(_2), .in3(_3), .in4(_4), .in5(_5), .in6(_6), .in7(_7), .in8(_8),
    .in9(_9), .in10(_10), .in11(_11), .in12(_12), .in13(_13), .in14(_14), .in15(_15), .in16(_16), .in17(_17),
    .in18(_18), .in19(_19), .in20(_20), .in21(_21), .in22(_22), .in23(_23), .in24(_24), .in25(_25),
    .in26(_26), .in27(_27), .in28(_28), .in29(_29), .in30(_30), .in31(_31), .out(RD2), .sel(A2));  // open: en
endmodule

module Control (
  input  [5:0] op,
  output RegDst,
  output MemWrite,
  output nPC_sel,
  output [1:0] ALUOp,
  output need_ALUC,
  output [1:0] ExtOp,
  output need_j,
  output need__pc_to_ra,
  output MemtoReg,
  output Regwrite,
  output ALUSrc
);

  wire beq_out, jal_out, lui_out, lw_out, not_1_out, not_2_out, not_3_out, not_4_out, not_5_out, not_6_out,
       ori_out, R_out, sw_out;

  not not_1 (not_1_out, op[5]);
  not not_2 (not_2_out, op[4]);
  not not_3 (not_3_out, op[3]);
  not not_4 (not_4_out, op[1]);
  not not_5 (not_5_out, op[2]);
  not not_6 (not_6_out, op[0]);
  and R (R_out, not_1_out, not_2_out, not_3_out, not_5_out, not_4_out, not_6_out);
  and ori (ori_out, not_1_out, not_2_out, op[3], op[2], not_4_out, op[0]);
  and lw (lw_out, op[5], not_2_out, not_3_out, not_5_out, op[1], op[0]);
  and sw (sw_out, op[5], not_2_out, op[3], not_5_out, op[1], op[0]);
  and beq (beq_out, not_1_out, not_2_out, not_3_out, op[2], not_4_out, not_6_out);
  and lui (lui_out, not_1_out, not_2_out, op[3], op[2], op[1], op[0]);
  and jal (jal_out, not_1_out, not_2_out, not_3_out, not_5_out, op[1], op[0]);
  buf or_1 (RegDst, R_out);  // OR_Gate
  or or_2 (ALUSrc, ori_out, sw_out, lw_out, lui_out);
  buf or_3 (MemtoReg, lw_out);  // OR_Gate
  or or_4 (Regwrite, R_out, ori_out, lw_out, jal_out, lui_out);
  buf or_5 (MemWrite, sw_out);  // OR_Gate
  buf or_6 (nPC_sel, beq_out);  // OR_Gate
  buf EXT1 (ExtOp[1], lui_out);  // OR_Gate
  or EXT0 (ExtOp[0], sw_out, lw_out);
  buf or_7 (need_ALUC, R_out);  // OR_Gate
  LED _10 (.in(ori_out));
  LED _00 (.in(lw_out));
  LED _00_2 (.in(sw_out));
  LED _01 (.in(beq_out));
  buf ALU1 (ALUOp[1], ori_out);  // OR_Gate
  buf ALU0 (ALUOp[0], beq_out);  // OR_Gate
  buf or_8 (need_j, jal_out);  // OR_Gate
  buf or_9 (need__pc_to_ra, jal_out);  // OR_Gate

  // Notes on the sheet:
  //   0means alunumB is from GRF1means alunumB is imm
  //   0means write GRF is 2threg in Instr rt 1means is 3th rd
  //   WE of GRF
  //   WE of DM
  //   0means write data GRF is from ALU 1:write GRF is DM
  //   EXTOP00zero_ext_01arithmetic_ext_10left_shift16b
  //   ALUOP00+01-10OR
endmodule

module ALU (
  input  [31:0] A,
  input  [31:0] B,
  input  [1:0] ALUOp,
  output [31:0] out,
  output zero
);

  wire [31:0] adder_1_out, or_1_out, subtractor_1_out;

  // Probe on A
  // Probe on B
  Adder #(.width(32)) adder_1 (.a(A), .b(B), .out(adder_1_out));  // open: cin, cout
  Subtractor #(.width(32)) subtractor_1 (.a(A), .b(B), .out(subtractor_1_out));  // open: bin, bout
  Comparator #(.width(32)) comparator_1 (.a(A), .b(B), .eq(zero));  // open: gt, lt
  assign or_1_out = A | B;  // OR_Gate or_1, 32 bits wide
  Multiplexer #(.select(2), .width(32)) multiplexer_1 (
    .in0(adder_1_out), .in1(subtractor_1_out), .in2(or_1_out), .out(out), .sel(ALUOp));  // open: in3, en
  // Probe on out
endmodule

module Data_Memory (
  input  [31:0] WData,
  input  ReadEn,
  input  WriteEn,
  input  CLK,
  input  [31:0] Address,
  input  CLR,
  output [31:0] outDATA,
  output [4:0] MemAddr
);

  // Probe on Address
  // Probe on Address
  RAM #(.addrWidth(5), .dataWidth(32), .bus("separate")) ram_1 (
    .addr(Address[6:2]), .din(WData), .data(outDATA), .str(WriteEn), .clk(CLK), .clr(CLR));  // open: sel, ld

  assign MemAddr = Address[6:2];
endmodule

module sign_EXT (
  input  [15:0] immin,
  input  [1:0] EXTOp,
  output [31:0] Result
);

  wire [31:0] bit_extender_1_out, bit_extender_2_out;

  // Probe on immin
  assign bit_extender_1_out = {{16{1'b0}}, immin};  // Bit_Extender bit_extender_1
  assign bit_extender_2_out = {{16{immin[15]}}, immin};  // Bit_Extender bit_extender_2
  Multiplexer #(.select(2), .width(32)) multiplexer_1 (
    .in0(bit_extender_1_out), .in1(bit_extender_2_out), .in2({immin, {16{1'b0}}}), .out(Result), .sel(EXTOp));  // open: in3, en
  // Probe on Result
  // Probe on Result
  // Probe on Result
endmodule

module PC (
  input  [31:0] PCin_next,
  input  CLK,
  input  CLR,
  output [31:0] PC_4,
  output [31:0] PCnow
);

  // Probe on PCnow
  // Probe on PCin_next
  Register #(.width(32)) register_1 (.D(PCin_next), .Q(PCnow), .clk(CLK), .clr(CLR));  // open: en
  Adder #(.width(32)) adder_1 (.a(32'h4), .b(PCnow), .out(PC_4));  // open: cin, cout
endmodule

module Instruction_Memory (
  input  [31:0] program_counter_address,
  output [15:0] imm,
  output [5:0] funct,
  output [4:0] shamt,
  output [4:0] rd,
  output [4:0] rt,
  output [4:0] rs,
  output [5:0] Op,
  output [31:0] Instr,
  output [25:0] instr_index
);

  // Probe on program_counter_address
  // Probe on program_counter_address[6:2]
  // Probe on program_counter_address[6:2]
  // Probe on {Instr[31:16], imm[15:6], funct}
  ROM #(.addrWidth(5), .dataWidth(32)) rom_1 (
    .addr(program_counter_address[6:2]), .data({Instr[31:16], imm[15:6], funct}));  // open: sel
  // Probe on {imm[15:6], funct}
  // Probe on {imm[15:6], funct}
  // Probe on {imm[15:6], funct}
  // Probe on funct
  // Probe on imm[15:11]
  // Probe on Instr[20:16]
  // Probe on Instr[25:21]
  // Probe on Instr[31:26]

  assign imm[5:0] = funct;
  assign Instr[15:0] = {imm[15:6], funct};
  assign instr_index = {Instr[25:16], imm[15:6], funct};
  assign Op = Instr[31:26];
  assign rd = imm[15:11];
  assign rs = Instr[25:21];
  assign rt = Instr[20:16];
  assign shamt = imm[10:6];

  // Notes on the sheet:
  //   contents of rom_1 (hex, n*v repeats v):
  //   12110001 35290001 35410001
  //   sw ==offset 
endmodule

module ALUControl (
  input  [5:0] func,
  output [1:0] ALUOp
);

  wire addu_out, ALU1_out, nop_out, not_1_out, not_2_out, not_3_out, not_4_out, not_5_out, not_6_out, sub_out;

  not not_1 (not_1_out, func[5]);
  not not_2 (not_2_out, func[4]);
  not not_3 (not_3_out, func[2]);
  not not_4 (not_4_out, func[3]);
  not not_5 (not_5_out, func[0]);
  not not_6 (not_6_out, func[1]);
  and addu (addu_out, func[5], not_2_out, not_4_out, not_3_out, not_6_out, func[0]);
  and sub (sub_out, func[5], not_2_out, not_4_out, not_3_out, func[1], func[0]);
  and nop (nop_out, func[5], func[4], func[3], func[2], func[1], func[0]);
  LED _00 (.in(addu_out));
  // OR_Gate ALU1 has open pins: out=ALU1_out
  buf ALU0 (ALUOp[0], sub_out);  // OR_Gate
  LED _01 (.in(sub_out));

  assign ALUOp[1] = 1'b0;

  // Notes on the sheet:
  //   This is not necessary
  //   ALUOP00+01-10OR
endmodule
